// Logisim project v1 Main 18 bit.circ as structural Verilog: 1 circuit, main circuit main
module main (
  input  in_1,
  input  in_2,
  input  in_3,
  input  in_4,
  output [3:0] RD__Immediate,
  output [3:0] RT,
  output [3:0] RS,
  output [17:0] Data_Read_2,
  output [3:0] OP,
  output [17:0] Output,
  output [1:0] Function,
  output [17:0] Data_Read_1,
  output [17:0] Address,
  output [17:0] Instructions,
  output [6:0] out_15,
  output [17:0] overflow
);

  wire and_1_out, bit_extender_5_out, clk, cu_aluClt, lw, main_1_cu_bne, main_3_p5, not_1_out, R_D, R_I, R_W,
       Res_Mem, sl, sw;
  wire [1:0] AluOp, multiplexer_3_out;
  wire [3:0] multiplexer_1_out;
  wire [6:0] bit_extender_2_out, bit_extender_3_out, shifter_1_out;
  wire [17:0] adder_1_out, Address_t, bit_extender_4_out, cu_bne, main_4_out_7, multiplexer_2_out,
       ram_1_data, register_1_q, shifter_2_out;

  Register #(.width(18)) register_1 (.D(Address_t), .Q(register_1_q), .clk(clk), .clr(in_4));  // open: en
  Clock clock_1 (.out(clk));
  v6_Control_Unit_main main_1 (
    .A(Instructions[13]), .B(Instructions[12]), .R_D(R_D), .R_W(R_W), .SW(sw), .SL(sl), .LW(lw),
    .Res_Mem(Res_Mem), .ALU_OP1(AluOp[1]), .Cu_BNE(main_1_cu_bne), .Cu_aluClt(cu_aluClt), .ALU_OP0(AluOp[0]),
    .R_I(R_I));
  assign cu_bne = {{17{1'b0}}, main_1_cu_bne};  // Bit_Extender bit_extender_1
  Adder #(.width(18)) adder_1 (.a(register_1_q), .b(18'h1), .out(adder_1_out));  // open: cin, cout
  ROM #(.addrWidth(18), .dataWidth(18)) rom_1 (
    .addr(register_1_q), .data({Function, Instructions[15:0]}));  // open: sel
  assign bit_extender_2_out = {{3{1'b0}}, Instructions[3:0]};  // Bit_Extender bit_extender_2
  assign bit_extender_3_out = {{5{1'b0}}, Function};  // Bit_Extender bit_extender_3
  Shifter #(.width(7)) shifter_1 (.in(bit_extender_2_out), .\dist (3'b100), .out(shifter_1_out));
  Adder #(.width(7)) adder_2 (.a(shifter_1_out), .b(bit_extender_3_out), .out(out_15));  // open: cin, cout
  Multiplexer #(.width(4), .enable("false")) multiplexer_1 (
    .in0(Instructions[7:4]), .in1(Instructions[3:0]), .out(multiplexer_1_out), .sel(R_D));
  assign bit_extender_4_out = {{11{1'b0}}, out_15};  // Bit_Extender bit_extender_4
  v3_REG_18_bit__main main_2 (
    .Data_in(Output), .enable(R_W), .Data_Address(multiplexer_1_out), .clk(clk), .Data01(Data_Read_1),
    .Data02(Data_Read_2), .RS(Instructions[11:8]), .RT(Instructions[7:4]));
  Multiplexer #(.width(18), .enable("false")) multiplexer_2 (
    .in0(Data_Read_2), .in1(bit_extender_4_out), .out(multiplexer_2_out), .sel(R_I));
  Multiplexer #(.width(2), .enable("false")) multiplexer_3 (
    .in0(Function), .in1(AluOp), .out(multiplexer_3_out), .sel(cu_aluClt));
  Shifter #(.width(18)) shifter_2 (.in(bit_extender_4_out), .\dist (5'b00001), .out(shifter_2_out));
  Bit_Extender #(.in_width(18), .out_width(1)) bit_extender_5 (.in(cu_bne), .out(bit_extender_5_out));
  // v1_ALU_18_bit_main main_3: pin names not known; wires that end beside it: Data_Read_1, multiplexer_2_out, multiplexer_3_out, in_2, main_3_p5, Address, overflow
  and and_1 (and_1_out, bit_extender_5_out, not_1_out);
  not not_1 (not_1_out, main_3_p5);
  v3_ALU_18_bit_main main_4 (
    .out_7(main_4_out_7), .c_in(in_1), .A(adder_1_out), .B(shifter_2_out), .OP_code(2'b10));  // open: ZERO, overflow_sum, sum_carry, c_in_sub, sub_carry
  Multiplexer #(.width(18), .enable("false")) multiplexer_4 (
    .in0(adder_1_out), .in1(main_4_out_7), .out(Address_t), .sel(and_1_out));
  Multiplexer #(.width(18), .enable("false")) multiplexer_5 (
    .in0(Address), .in1(ram_1_data), .out(Output), .sel(Res_Mem));
  RAM #(.addrWidth(18), .dataWidth(18), .bus("separate")) ram_1 (
    .addr(Address), .din(Data_Read_2), .data(ram_1_data), .str(sw), .sel(sl), .clk(clk), .ld(lw), .clr(in_3));

  assign Instructions[17:16] = Function;
  assign OP = Instructions[15:12];
  assign RD__Immediate = Instructions[3:0];
  assign RS = Instructions[11:8];
  assign RT = Instructions[7:4];

  // Other names for the same wires on the sheet: D_in[17:0] = Output; Imm[6:0] = out_15; RD[3:0] = Instructions[3:0];
  //   cu_[3:0] = Instructions[15:12]

  // Notes on the sheet:
  //   contents of rom_1 (hex, n*v repeats v):
  //   12 10345 20678 13010
endmodule
