// Logisim project v1 pipeline Main 18 bit.circ as structural Verilog: 1 circuit, main circuit main
module main (
  input  in_1,
  input  in_2,
  input  in_3,
  input  in_4,
  output [3:0] RD__Immediate,
  output [3:0] RT,
  output [3:0] RS,
  output [17:0] Output,
  output [17:0] Data_Read_2,
  output [3:0] OP,
  output [1:0] Function,
  output [17:0] Data_Read_1,
  output [17:0] Address,
  output [17:0] Instructions,
  output [6:0] out_15,
  output [1:0] out_16
);

  wire and_1_out, bit_extender_3_out, clk, cu_aluClt, lw, main_1_cu_aluclt, main_1_cu_bne, main_1_lw,
       main_1_r_d, main_1_r_i, main_1_r_w, main_1_res_mem, main_1_sl, main_1_sw, main_3_p5, not_1_out, R_D,
       R_I, R_W, register_8_q, register_9_q, register_10_q, register_11_q, register_12_q, register_13_q,
       register_14_q, register_15_q, register_20_q, register_21_q, register_23_q, register_25_q,
       register_28_q, register_38_q, register_39_q, Res_Mem, sl, sw;
  wire [1:0] AluOp, register_33_q, register_34_q;
  wire [3:0] multiplexer_1_out, rd_2, register_4_q, register_6_q;
  wire [6:0] bit_extender_4_out, bit_extender_5_out, shifter_2_out;
  wire [17:0] Add_to_mux, Address_t, bit_extender_1_out, bit_extender_2_out, cu_bne, main_3_p6, main_4_out_7,
       multiplexer_2_out, ram_1_data, register_1_q, register_2_q, register_29_q, register_30_q,
       register_31_q, register_32_q, register_36_q, register_37_q, register_40_q, register_41_q,
       shifter_1_out;

  Clock clock_1 (.out(clk));
  Register #(.width(18)) register_1 (.D(Address_t), .Q(register_1_q), .clk(clk), .clr(in_4));  // open: en
  Adder #(.width(18)) adder_1 (.a(register_1_q), .b(18'h1), .out(Add_to_mux));  // open: cin, cout
  v6_Control_Unit_main main_1 (
    .A(OP[1]), .B(OP[0]), .R_D(main_1_r_d), .R_W(main_1_r_w), .SW(main_1_sw), .SL(main_1_sl), .LW(main_1_lw),
    .Res_Mem(main_1_res_mem), .ALU_OP1(AluOp[1]), .Cu_BNE(main_1_cu_bne), .Cu_aluClt(main_1_cu_aluclt),
    .ALU_OP0(AluOp[0]), .R_I(main_1_r_i));
  ROM #(.addrWidth(18), .dataWidth(18)) rom_1 (.addr(register_1_q), .data(Instructions));  // open: sel
  assign bit_extender_1_out = {{17{1'b0}}, main_1_cu_bne};  // Bit_Extender bit_extender_1
  Register #(.width(18)) register_2 (.D(Add_to_mux), .Q(register_2_q), .clk(clk), .clr(in_4));  // open: en
  Register #(.width(18)) register_3 (
    .D(Instructions), .Q({Function, OP, RS, RT, RD__Immediate}), .clk(clk), .clr(in_4));  // open: en
  Register #(.width(4)) register_4 (.D(RD__Immediate), .Q(register_4_q), .clk(clk), .clr(in_4));  // open: en
  Register #(.width(1)) register_5 (.D(main_1_r_i), .Q(R_I), .clk(clk), .clr(in_4));  // open: en
  Register #(.width(4)) register_6 (.D(register_4_q), .Q(register_6_q), .clk(clk), .clr(in_4));  // open: en
  Register #(.width(4)) register_7 (.D(register_6_q), .Q(rd_2), .clk(clk), .clr(in_4));  // open: en
  Register #(.width(1)) register_8 (.D(register_9_q), .Q(register_8_q), .clk(clk), .clr(in_4));  // open: en
  Register #(.width(1)) register_9 (.D(main_1_r_d), .Q(register_9_q), .clk(clk), .clr(in_4));  // open: en
  Register #(.width(1)) register_10 (.D(main_1_r_w), .Q(register_10_q), .clk(clk), .clr(in_4));  // open: en
  Register #(.width(1)) register_11 (.D(register_10_q), .Q(register_11_q), .clk(clk), .clr(in_4));  // open: en
  Register #(.width(1)) register_12 (.D(main_1_sw), .Q(register_12_q), .clk(clk), .clr(in_4));  // open: en
  Register #(.width(1)) register_13 (.D(main_1_sl), .Q(register_13_q), .clk(clk), .clr(in_4));  // open: en
  Register #(.width(1)) register_14 (.D(main_1_lw), .Q(register_14_q), .clk(clk), .clr(in_4));  // open: en
  Register #(.width(1)) register_15 (.D(main_1_cu_aluclt), .Q(register_15_q), .clk(clk), .clr(in_4));  // open: en
  Register #(.width(1)) register_16 (.D(register_15_q), .Q(cu_aluClt), .clk(clk), .clr(in_4));  // open: en
  Multiplexer #(.width(4), .enable("false")) multiplexer_1 (.in0(RT), .in1(rd_2), .out(multiplexer_1_out), .sel(R_D));
  Register #(.width(1)) register_17 (.D(register_8_q), .Q(R_D), .clk(clk), .clr(in_4));  // open: en
  Register #(.width(1)) register_18 (.D(register_11_q), .Q(R_W), .clk(clk), .clr(in_4));  // open: en
  Register #(.width(1)) register_19 (.D(register_20_q), .Q(sw), .clk(clk), .clr(in_4));  // open: en
  Register #(.width(1)) register_20 (.D(register_12_q), .Q(register_20_q), .clk(clk), .clr(in_4));  // open: en
  Register #(.width(1)) register_21 (.D(register_13_q), .Q(register_21_q), .clk(clk), .clr(in_4));  // open: en
  Register #(.width(1)) register_22 (.D(register_21_q), .Q(sl), .clk(clk), .clr(in_4));  // open: en
  Register #(.width(1)) register_23 (.D(register_14_q), .Q(register_23_q), .clk(clk), .clr(in_4));  // open: en
  Register #(.width(1)) register_24 (.D(register_23_q), .Q(lw), .clk(clk), .clr(in_4));  // open: en
  Register #(.width(1)) register_25 (.D(main_1_res_mem), .Q(register_25_q), .clk(clk), .clr(in_4));  // open: en
  Register #(.width(18)) register_26 (.D(bit_extender_1_out), .Q(cu_bne), .clk(clk), .clr(in_4));  // open: en
  Register #(.width(1)) register_27 (.D(register_28_q), .Q(Res_Mem), .clk(clk), .clr(in_4));  // open: en
  Register #(.width(1)) register_28 (.D(register_25_q), .Q(register_28_q), .clk(clk), .clr(in_4));  // open: en
  v3_REG_18_bit__main main_2 (
    .Data_in(Output), .enable(R_W), .Data_Address(multiplexer_1_out), .clk(clk), .Data01(Data_Read_1),
    .Data02(Data_Read_2), .RS(RS), .RT(RT));
  assign bit_extender_2_out = {{11{1'b0}}, out_15};  // Bit_Extender bit_extender_2
  Register #(.width(18)) register_29 (.D(register_2_q), .Q(register_29_q), .clk(clk), .clr(in_4));  // open: en
  Register #(.width(18)) register_30 (.D(Data_Read_1), .Q(register_30_q), .clk(clk), .clr(in_4));  // open: en
  Register #(.width(18)) register_31 (.D(Data_Read_2), .Q(register_31_q), .clk(clk), .clr(in_4));  // open: en
  Register #(.width(18)) register_32 (.D(bit_extender_2_out), .Q(register_32_q), .clk(clk), .clr(in_4));  // open: en
  Multiplexer #(.width(18), .enable("false")) multiplexer_2 (
    .in0(register_31_q), .in1(register_32_q), .out(multiplexer_2_out), .sel(R_I));
  Register #(.width(2)) register_33 (.D(Function), .Q(register_33_q), .clk(clk), .clr(in_4));  // open: en
  Register #(.width(2)) register_34 (.D(AluOp), .Q(register_34_q), .clk(clk), .clr(in_4));  // open: en
  Multiplexer #(.width(2), .enable("false")) multiplexer_3 (
    .in0(register_33_q), .in1(register_34_q), .out(out_16), .sel(cu_aluClt));
  Shifter #(.width(18)) shifter_1 (.in(register_32_q), .\dist (5'b00001), .out(shifter_1_out));
  Bit_Extender #(.in_width(18), .out_width(1)) bit_extender_3 (.in(cu_bne), .out(bit_extender_3_out));
  // v1_ALU_18_bit_main main_3: pin names not known; wires that end beside it: register_30_q, multiplexer_2_out, out_16, in_2, main_3_p5, main_3_p6
  and and_1 (and_1_out, bit_extender_3_out, not_1_out);
  not not_1 (not_1_out, main_3_p5);
  Register #(.width(18)) register_35 (.D(main_3_p6), .Q(Address), .clk(clk), .clr(in_4));  // open: en
  Register #(.width(18)) register_36 (.D(Data_Read_2), .Q(register_36_q), .clk(clk), .clr(in_4));  // open: en
  v3_ALU_18_bit_main main_4 (
    .out_7(main_4_out_7), .c_in(in_1), .A(register_29_q), .B(shifter_1_out), .OP_code(2'b10));  // open: ZERO, overflow_sum, sum_carry, c_in_sub, sub_carry
  assign bit_extender_4_out = {{3{1'b0}}, RD__Immediate};  // Bit_Extender bit_extender_4
  assign bit_extender_5_out = {{5{1'b0}}, Function};  // Bit_Extender bit_extender_5
  Register #(.width(18)) register_37 (.D(main_4_out_7), .Q(register_37_q), .clk(clk), .clr(in_4));  // open: en
  Register #(.width(1)) register_38 (.D(register_39_q), .Q(register_38_q), .clk(clk), .clr(in_4));  // open: en
  Register #(.width(1)) register_39 (.D(and_1_out), .Q(register_39_q), .clk(clk), .clr(in_4));  // open: en
  Multiplexer #(.width(18), .enable("false")) multiplexer_4 (
    .in0(Add_to_mux), .in1(register_37_q), .out(Address_t), .sel(register_38_q));
  Shifter #(.width(7)) shifter_2 (.in(bit_extender_4_out), .\dist (3'b100), .out(shifter_2_out));
  Register #(.width(18)) register_40 (.D(Address), .Q(register_40_q), .clk(clk), .clr(in_4));  // open: en
  RAM #(.addrWidth(18), .dataWidth(18), .bus("separate")) ram_1 (
    .addr(Address), .din(register_36_q), .data(ram_1_data), .str(sw), .sel(sl), .clk(clk), .ld(lw), .clr(in_3));
  Register #(.width(18)) register_41 (.D(ram_1_data), .Q(register_41_q), .clk(clk), .clr(in_4));  // open: en
  Adder #(.width(7)) adder_2 (.a(shifter_2_out), .b(bit_extender_5_out), .out(out_15));  // open: cin, cout
  Multiplexer #(.width(18), .enable("false")) multiplexer_5 (
    .in0(register_40_q), .in1(register_41_q), .out(Output), .sel(Res_Mem));

  // Other names for the same wires on the sheet: RD[3:0] = RD__Immediate; rd_1[3:0] = RD__Immediate; cu_[3:0] = OP;
  //   _0 = in_4; D_in[17:0] = Output; Imm[6:0] = out_15

  // Notes on the sheet:
  //   contents of rom_1 (hex, n*v repeats v):
  //   234 10567 2089a 13010
endmodule
