// Logisim project v3 REG 18 bit .circ as structural Verilog: 1 circuit, main circuit main
module main (
  input  [17:0] Data_in,
  input  enable,
  input  [3:0] RS,
  input  [3:0] Data_Address,
  input  clk,
  input  [3:0] RT,
  output [17:0] Data01,
  output [17:0] Data02
);

  wire demultiplexer_1_out0, demultiplexer_1_out1, demultiplexer_1_out2, demultiplexer_1_out3,
       demultiplexer_1_out4, demultiplexer_1_out5, demultiplexer_1_out6, demultiplexer_1_out7,
       demultiplexer_1_out8, demultiplexer_1_out9, demultiplexer_1_out10, demultiplexer_1_out11,
       demultiplexer_1_out12, demultiplexer_1_out13, demultiplexer_1_out14, demultiplexer_1_out15;
  wire [17:0] register_1_q, register_2_q, register_3_q, register_4_q, register_5_q, register_6_q,
       register_7_q, register_8_q, register_9_q, register_10_q, register_11_q, register_12_q, register_13_q,
       register_14_q, register_15_q, register_16_q;

  Demultiplexer #(.select(4)) demultiplexer_1 (
    .out0(demultiplexer_1_out0), .out1(demultiplexer_1_out1), .out2(demultiplexer_1_out2),
    .out3(demultiplexer_1_out3), .out4(demultiplexer_1_out4), .out5(demultiplexer_1_out5),
    .out6(demultiplexer_1_out6), .out7(demultiplexer_1_out7), .out8(demultiplexer_1_out8),
    .out9(demultiplexer_1_out9), .out10(demultiplexer_1_out10), .out11(demultiplexer_1_out11),
    .out12(demultiplexer_1_out12), .out13(demultiplexer_1_out13), .out14(demultiplexer_1_out14),
    .out15(demultiplexer_1_out15), .in(enable), .sel(Data_Address));  // open: en
  Register #(.width(18)) register_1 (.D(Data_in), .en(demultiplexer_1_out0), .Q(register_1_q), .clk(clk));  // open: clr
  Register #(.width(18)) register_2 (.D(Data_in), .en(demultiplexer_1_out1), .Q(register_2_q), .clk(clk));  // open: clr
  Register #(.width(18)) register_3 (.D(Data_in), .en(demultiplexer_1_out2), .Q(register_3_q), .clk(clk));  // open: clr
  Register #(.width(18)) register_4 (.D(Data_in), .en(demultiplexer_1_out3), .Q(register_4_q), .clk(clk));  // open: clr
  Register #(.width(18)) register_5 (.D(Data_in), .en(demultiplexer_1_out4), .Q(register_5_q), .clk(clk));  // open: clr
  Register #(.width(18)) register_6 (.D(Data_in), .en(demultiplexer_1_out5), .Q(register_6_q), .clk(clk));  // open: clr
  Register #(.width(18)) register_7 (.D(Data_in), .en(demultiplexer_1_out6), .Q(register_7_q), .clk(clk));  // open: clr
  Register #(.width(18)) register_8 (.D(Data_in), .en(demultiplexer_1_out7), .Q(register_8_q), .clk(clk));  // open: clr
  Register #(.width(18)) register_9 (.D(Data_in), .en(demultiplexer_1_out8), .Q(register_9_q), .clk(clk));  // open: clr
  Register #(.width(18)) register_10 (
    .D(Data_in), .en(demultiplexer_1_out9), .Q(register_10_q), .clk(clk));  // open: clr
  Register #(.width(18)) register_11 (
    .D(Data_in), .en(demultiplexer_1_out10), .Q(register_11_q), .clk(clk));  // open: clr
  Register #(.width(18)) register_12 (
    .D(Data_in), .en(demultiplexer_1_out11), .Q(register_12_q), .clk(clk));  // open: clr
  Register #(.width(18)) register_13 (
    .D(Data_in), .en(demultiplexer_1_out12), .Q(register_13_q), .clk(clk));  // open: clr
  Register #(.width(18)) register_14 (
    .D(Data_in), .en(demultiplexer_1_out13), .Q(register_14_q), .clk(clk));  // open: clr
  Register #(.width(18)) register_15 (
    .D(Data_in), .en(demultiplexer_1_out14), .Q(register_15_q), .clk(clk));  // open: clr
  Register #(.width(18)) register_16 (
    .D(Data_in), .en(demultiplexer_1_out15), .Q(register_16_q), .clk(clk));  // open: clr
  Multiplexer #(.select(4), .width(18)) multiplexer_1 (
    .in0(register_1_q), .in1(register_2_q), .in2(register_3_q), .in3(register_4_q), .in4(register_5_q),
    .in5(register_6_q), .in6(register_7_q), .in7(register_8_q), .in8(register_9_q), .in9(register_10_q),
    .in10(register_11_q), .in11(register_12_q), .in12(register_13_q), .in13(register_14_q),
    .in14(register_15_q), .in15(register_16_q), .out(Data01), .sel(RS));  // open: en
  Multiplexer #(.select(4), .width(18)) multiplexer_2 (
    .in0(register_1_q), .in1(register_2_q), .in2(register_3_q), .in3(register_4_q), .in4(register_5_q),
    .in5(register_6_q), .in6(register_7_q), .in7(register_8_q), .in8(register_9_q), .in9(register_10_q),
    .in10(register_11_q), .in11(register_12_q), .in12(register_13_q), .in13(register_14_q),
    .in14(register_15_q), .in15(register_16_q), .out(Data02), .sel(RT));  // open: en
endmodule
