// Logisim project v6 Control Unit.circ as structural Verilog: 1 circuit, main circuit main
module main (
  input  B,
  input  A,
  output R_D,
  output R_W,
  output R_I,
  output SW,
  output SL,
  output LW,
  output Res_Mem,
  output ALU_OP1,
  output ALU_OP0,
  output Cu_BNE,
  output Cu_aluClt
);

  wire not_2_out;

  not not_1 (R_D, B);
  not not_2 (not_2_out, A);
  and and_1 (R_I, not_2_out, B);

  assign ALU_OP0 = 1'b1;
  assign ALU_OP1 = 1'b1;
  assign Cu_aluClt = B;
  assign Cu_BNE = B;
  assign LW = 1'b0;
  assign R_W = 1'b1;
  assign Res_Mem = 1'b0;
  assign SL = 1'b0;
  assign SW = 1'b0;
endmodule
